# Fritzing sketch Schematic (saved by Fritzing 1.0.1rc)

parts:
  U1 = ESP32-38PinWide [part_number=ESP32-38PinWide]
  Door_Relay = WeMos D1 Mini Relay Shield V2
  Video_Relay = WeMos D1 Mini Relay Shield V2
  U3 = LIPO-1000mAh [package=lipo-1000]  # not connected
  VCC1 = Battery block 9V  # not connected

nets:
  N1: U1.GPIO4, Video_Relay.D0
  N2: U1.GPIO5, Door_Relay.D0

custom parts:
  ESP32-38PinWide: Generic 38-Pin ESP32 with wide format (only access to one side of pins on a breadboard) based on Stephen Lilley's HiLetgo ESP-WROOM-32 ESP32 ESP-32S Development Board.
