# Fritzing sketch Schematic (saved by Fritzing 0.9.5d)

parts:
  U1 = ESP32-38PinWide [part_number=ESP32-38PinWide]
  Door_Relay = WeMos D1 Mini Relay Shield V2
  Video_Relay = WeMos D1 Mini Relay Shield V2
  U3 = LIPO-1000mAh [package=lipo-1000]
  BAT1 = BC9VPC [package=bc9vpc]

nets:
  N1: U1.3.3, U3.+
  N2: U1.GND, Door_Relay.G, Video_Relay.G, U3.-, BAT1.V-
  N3: U1.GPIO4, Video_Relay.D0
  N4: U1.GPIO5, Door_Relay.D0
  5V: Door_Relay.5V, Video_Relay.5V, BAT1.V+

notes:
  aquí se encontraría la PCB con los botones

custom parts:
  ESP32-38PinWide: Generic 38-Pin ESP32 with wide format (only access to one side of pins on a breadboard) based on Stephen Lilley's HiLetgo ESP-WROOM-32 ESP32 ESP-32S Development Board.
